// Logisim project alu-control.circ as structural Verilog: 2 circuits, main circuit main
module main (
  input  [1:0] Opcode,
  input  [5:0] Funct,
  input  [1:0] sh,
  output [3:0] ALUControl
);


  // Other names for the same wires on the sheet: Ctrl[3:0] = ALUControl; FN[5:0] = Funct; OP[1:0] = Opcode

  // Notes on the sheet:
  //   DO NOT MOVE, CHANGE, ADD, OR REMOVE INPUTS AND OUTPUTS!!!
endmodule

module data_processing (
  input  [1:0] sh,
  input  [5:0] Funct,
  input  [1:0] OP,
  output [3:0] ALUControl
);

  wire undriven;

  Multiplexer #(.select(2), .width(4)) multiplexer_1 (
    .in0(4'b0100), .in1(4'b0101), .in2(4'b0110), .out(ALUControl), .sel(sh), .en(1'b1));  // open: in3
  Multiplexer #(.select(4), .width(4)) multiplexer_2 (
    .in0(4'b0000), .in1(4'b0010), .in2(4'b1000), .in4(4'b0111), .in10(4'b1000), .in12(4'b0001),
    .in13(4'b1101), .in15(4'b0011), .out(ALUControl), .sel(Funct[4:1]), .en(undriven));  // open: in3, in5, in6, in7, in8, in9, in11, in14
  Multiplexer #(.select(2), .enable("false")) multiplexer_3 (.in0(undriven), .sel(OP));  // open: in1, in2, in3, out

  // Notes on the sheet:
  //   shifts instruction
  //   data-processing Instruction
endmodule
