// Logisim project alu.circ as structural Verilog
module main (
  input  [31:0] A,
  input  [31:0] B,
  input  [3:0] ALUControl,
  output [3:0] ALUFlags,
  output [31:0] Result
);

  wire adder_1_cout, subtractor_1_bout, undriven_2, xor_1_out;
  wire [31:0] add, \and , asr, lsl, lsr, \not , \or , sub, \xor ;
  wire [31:31] undriven;

  Multiplexer #(.select(4), .width(32), .enable("false")) multiplexer_1 (
    .in0(\and ), .in1(\or ), .in2(\xor ), .in3(\not ), .in4(lsl), .in5(lsr), .in6(asr), .in7(add), .in8(sub),
    .out(Result), .sel(ALUControl));  // open: in9, in10, in11, in12, in13, in14, in15
  Comparator #(.width(32)) comparator_1 (.a(Result), .b({32{1'b0}}), .eq(ALUFlags[2]), .lt(ALUFlags[3]));  // open: gt
  assign \and  = A & B;  // AND_Gate _0000, 32 bits wide
  assign \or  = A | B;  // OR_Gate _0001, 32 bits wide
  assign \not  = ~A;  // NOT_Gate _0011, 32 bits wide
  Shifter #(.width(32)) shifter_1 (.in(A), .\dist (B[4:0]), .out(lsl));
  Shifter #(.width(32), .shift("lr")) shifter_2 (.in(A), .\dist (B[4:0]), .out(lsr));
  Shifter #(.width(32), .shift("ar")) shifter_3 (.in(A), .\dist (B[4:0]), .out(asr));
  Adder #(.width(32)) adder_1 (.a(A), .b(B), .out(add), .cout(adder_1_cout));  // open: cin
  Subtractor #(.width(32)) subtractor_1 (.a(A), .b(B), .out(sub), .bout(subtractor_1_bout));  // open: bin
  assign \xor  = A ^ B;  // XOR_Gate _0010, 32 bits wide
  or or_1 (ALUFlags[1], adder_1_cout, subtractor_1_bout);
  xor xor_1 (xor_1_out, A[31], undriven[31]);
  // AND_Gate and_1 has open pins: in0=undriven_2, in1=xor_1_out, out=open
  // XOR_Gate xor_2 is placed but not wired

  assign ALUFlags[0] = 1'b0;

  // Other names for the same wires on the sheet: Carry = ALUFlags[1]; Zero = ALUFlags[2]; Negative = ALUFlags[3];
  //   Ctrl[3:0] = ALUControl

  // Notes on the sheet:
  //   INPUTS to your circuit
  //   DON'T CHANGE THE LOCATIONS OF THE INPUTS AND OUTPUTS!
  //   OUTPUTS from your circuit
endmodule
